// Digital circuit cpu.dig as structural Verilog
module cpu (
  input  CLK,
  output [7:0] Ac,
  output [7:0] Mq
);

  wire DQ, Q;
  wire [2:0] OpC;
  wire [7:0] N, pc_1_addr;
  wire [10:0] rom_1_d;

  D_FF d_ff_1 (.D(Q), .C(CLK), .Q(DQ), .nQ(Q));
  ALU alu_1 (.N(N), .EN(DQ), .Clk(CLK), .Op(OpC), .AC(Ac), .MQ(Mq));
  PC pc_1 (.CLK(CLK), .EN(DQ), .ADDR(pc_1_addr));
  ROM #(.AddrBits(8), .Bits(11)) rom_1 (.A(pc_1_addr), .sel(Q), .D(rom_1_d));
  Register #(.Bits(11)) register_1 (.D(rom_1_d), .C(CLK), .en(Q), .Q({OpC, N}));
endmodule
